// Logisim project EP02.circ as structural Verilog: 5 circuits, main circuit MAIN
// MUX 4x2
module MUX (
  input  M,
  input  N,
  input  O,
  input  P,
  input  Op1,
  input  Op0,
  output S
);

  wire and_1_out, and_2_out, and_3_out, and_4_out, not_1_out, not_2_out, not_3_out, not_4_out;

  not not_1 (not_1_out, Op1);
  not not_2 (not_2_out, Op0);
  not not_3 (not_3_out, Op1);
  not not_4 (not_4_out, Op0);
  and and_1 (and_1_out, M, not_1_out, not_2_out);
  and and_2 (and_2_out, N, not_3_out, Op0);
  and and_3 (and_3_out, O, Op1, not_4_out);
  and and_4 (and_4_out, P, Op1, Op0);
  or or_1 (S, and_1_out, and_2_out, and_3_out, and_4_out);
endmodule

module MAIN (
  input  Binvert,
  input  B3,
  input  B2,
  input  B1,
  input  B0,
  input  A3,
  input  A2,
  input  A1,
  input  A0,
  input  OP1,
  input  OP0,
  output S0,
  output S1,
  output S2,
  output S3,
  output Cout
);

  wire ula_1bit_1_cout, ula_1bit_2_cout, ula_1bit_3_cout;

  ULA_1bit ula_1bit_1 (
    .A(A0), .B(B0), .S(S0), .Bivent(Binvert), .Cin(Binvert), .Cout(ula_1bit_1_cout), .Op1(OP1), .Op0(OP0));
  ULA_1bit ula_1bit_2 (
    .A(A1), .B(B1), .S(S1), .Bivent(Binvert), .Cin(ula_1bit_1_cout), .Cout(ula_1bit_2_cout), .Op1(OP1),
    .Op0(OP0));
  ULA_1bit ula_1bit_3 (
    .A(A2), .B(B2), .S(S2), .Bivent(Binvert), .Cin(ula_1bit_2_cout), .Cout(ula_1bit_3_cout), .Op1(OP1),
    .Op0(OP0));
  ULA_1bit ula_1bit_4 (
    .A(A3), .B(B3), .S(S3), .Bivent(Binvert), .Cin(ula_1bit_3_cout), .Cout(Cout), .Op1(OP1), .Op0(OP0));

  // Notes on the sheet:
  //   Cin
endmodule

module SOMA (
  input  A,
  input  B,
  input  Cin,
  output S,
  output Cout
);

  wire and_1_out, and_2_out, xor_1_out;

  xor xor_1 (xor_1_out, A, B);
  and and_1 (and_1_out, A, B);
  xor xor_2 (S, xor_1_out, Cin);
  and and_2 (and_2_out, xor_1_out, Cin);
  or or_1 (Cout, and_2_out, and_1_out);
endmodule

// ULA 1 bit
module ULA_1bit (
  input  Bivent,
  input  A,
  input  Cin,
  input  B,
  input  Op1,
  input  Op0,
  output S,
  output Cout
);

  wire and_1_out, mux_pequeno_1_s, not_1_out, not_2_out, or_1_out, soma_1_s;

  not not_1 (not_1_out, B);
  MUX_pequeno mux_pequeno_1 (.B(B), .S(mux_pequeno_1_s), .Bivent(Bivent), .nB(not_1_out));
  and and_1 (and_1_out, A, B);
  or or_1 (or_1_out, A, B);
  not not_2 (not_2_out, A);
  SOMA soma_1 (.A(A), .B(mux_pequeno_1_s), .Cin(Cin), .S(soma_1_s), .Cout(Cout));
  MUX mux_1 (.M(and_1_out), .N(or_1_out), .O(not_2_out), .P(soma_1_s), .S(S), .Op1(Op1), .Op0(Op0));
endmodule

// 1 0
module MUX_pequeno (
  input  Bivent,
  input  B,
  input  nB,
  output S
);

  wire and_1_out, and_2_out, not_1_out;

  and and_1 (and_1_out, B, not_1_out);
  not not_1 (not_1_out, Bivent);
  and and_2 (and_2_out, nB, Bivent);
  or or_1 (S, and_1_out, and_2_out);
endmodule
